// Logisim project modular_adder_subtractor_circuit.circ as structural Verilog: 5 circuits, main circuit main
module main (
  input  s,
  input  x3,
  input  y3,
  input  x2,
  input  y2,
  input  x1,
  input  y1,
  input  x0,
  input  y0,
  output z3,
  output z2,
  output z1,
  output z0
);

  wire a0_0, a0_1, a1_0, a1_1, a2_0, a2_1, a3_0, a3_1, and_1_out, and_2_out, b1_0, b1_1, b2_0, b2_1, b3_0,
       b3_1, b4, b4_0, b4_1, black_node_1_gigj, black_node_1_pipj, black_node_3_gigj, black_node_4_gigj,
       black_node_4_pipj, black_node_5_gigj, black_node_5_pipj, black_node_7_gigj, black_node_8_gigj,
       black_node_8_pipj, multiplexer_4_out, multiplexer_6_out, multiplexer_8_out, multiplexer_9_out,
       multiplexer_10_out, multiplexer_11_out, multiplexer_12_out, nor_1_out, not_1_out, or_1_out, or_2_out,
       precomputation_1_gi, precomputation_1_hi, precomputation_1_pi, precomputation_2_gi,
       precomputation_2_hi, precomputation_2_pi, precomputation_3_gi, precomputation_3_hi,
       precomputation_3_pi, precomputation_4_gi, precomputation_4_pi, precomputation_5_gi,
       precomputation_5_hi, precomputation_5_pi, precomputation_6_gi, precomputation_6_hi,
       precomputation_6_pi, precomputation_7_gi, precomputation_7_hi, precomputation_7_pi,
       precomputation_8_gi, precomputation_8_pi, V0, V1, V2, V3, V4, W0, W1, W2, W3, W4, xor_2_out,
       xor_5_out, xor_6_out, xor_9_out;

  precomputation precomputation_1 (
    .ai(a3_0), .bi(b3_0), .Hi(precomputation_1_hi), .Gi(precomputation_1_gi), .Pi(precomputation_1_pi));
  black_node black_node_1 (
    .Gi(precomputation_1_gi), .Gj(precomputation_2_gi), .Pi(precomputation_1_pi), .Pj(precomputation_2_pi),
    .GiGj(black_node_1_gigj), .PiPj(black_node_1_pipj));
  black_node black_node_2 (
    .Gi(black_node_1_gigj), .Gj(black_node_4_gigj), .Pi(black_node_1_pipj), .Pj(black_node_4_pipj), .GiGj(W4));  // open: PiPj
  xor xor_1 (W3, precomputation_1_hi, black_node_3_gigj);
  xor xor_2 (xor_2_out, y3, s);
  HAL hal_1 (.yi_xor_s(xor_2_out), .xi(x3), .Ai(a3_0), .NOT_Ai(a3_1), .Bj(b4_0), .NOT_Bj(b4_1));
  precomputation precomputation_2 (
    .ai(a2_0), .bi(b2_0), .Hi(precomputation_2_hi), .Gi(precomputation_2_gi), .Pi(precomputation_2_pi));
  black_node black_node_3 (
    .Gi(precomputation_2_gi), .Gj(black_node_4_gigj), .Pi(precomputation_2_pi), .Pj(black_node_4_pipj),
    .GiGj(black_node_3_gigj));  // open: PiPj
  xor xor_3 (W2, precomputation_2_hi, black_node_4_gigj);
  precomputation precomputation_3 (
    .ai(a1_0), .bi(b1_0), .Hi(precomputation_3_hi), .Gi(precomputation_3_gi), .Pi(precomputation_3_pi));
  black_node black_node_4 (
    .Gi(precomputation_3_gi), .Gj(precomputation_4_gi), .Pi(precomputation_3_pi), .Pj(precomputation_4_pi),
    .GiGj(black_node_4_gigj), .PiPj(black_node_4_pipj));
  xor xor_4 (W1, precomputation_3_hi, precomputation_4_gi);
  or or_1 (or_1_out, W4, b4_0);
  nor nor_1 (nor_1_out, V4, b4);
  HAL hal_2 (.yi_xor_s(xor_5_out), .xi(x2), .Ai(a2_0), .NOT_Ai(a2_1), .Bj(b3_0), .NOT_Bj(b3_1));
  not not_1 (not_1_out, s);
  xor xor_5 (xor_5_out, y2, s);
  precomputation precomputation_4 (.ai(a0_0), .bi(s), .Hi(W0), .Gi(precomputation_4_gi), .Pi(precomputation_4_pi));
  and and_1 (and_1_out, or_1_out, s);
  and and_2 (and_2_out, nor_1_out, not_1_out);
  or or_2 (or_2_out, and_1_out, and_2_out);
  Multiplexer multiplexer_1 (.in0(V3), .in1(W3), .out(z3), .sel(or_2_out));
  xor xor_6 (xor_6_out, y1, s);
  HAL hal_3 (.yi_xor_s(xor_6_out), .xi(x1), .Ai(a1_0), .NOT_Ai(a1_1), .Bj(b2_0), .NOT_Bj(b2_1));
  Multiplexer multiplexer_2 (.in0(b4_0), .in1(b4_1), .out(b4), .sel(s));
  Multiplexer multiplexer_3 (.in0(V2), .in1(W2), .out(z2), .sel(or_2_out));
  Multiplexer multiplexer_4 (.in0(a3_0), .in1(a3_1), .out(multiplexer_4_out), .sel(s));
  precomputation precomputation_5 (
    .ai(multiplexer_4_out), .bi(multiplexer_6_out), .Hi(precomputation_5_hi), .Gi(precomputation_5_gi),
    .Pi(precomputation_5_pi));
  xor xor_7 (V3, precomputation_5_hi, black_node_7_gigj);
  Multiplexer multiplexer_5 (.in0(V1), .in1(W1), .out(z1), .sel(or_2_out));
  Multiplexer multiplexer_6 (.in0(b3_1), .in1(b3_0), .out(multiplexer_6_out), .sel(s));
  black_node black_node_5 (
    .Gi(precomputation_5_gi), .Gj(precomputation_6_gi), .Pi(precomputation_5_pi), .Pj(precomputation_6_pi),
    .GiGj(black_node_5_gigj), .PiPj(black_node_5_pipj));
  black_node black_node_6 (
    .Gi(black_node_5_gigj), .Gj(black_node_8_gigj), .Pi(black_node_5_pipj), .Pj(black_node_8_pipj), .GiGj(V4));  // open: PiPj
  Multiplexer multiplexer_7 (.in0(V0), .in1(W0), .out(z0), .sel(or_2_out));
  Multiplexer multiplexer_8 (.in0(a2_1), .in1(a2_0), .out(multiplexer_8_out), .sel(s));
  precomputation precomputation_6 (
    .ai(multiplexer_8_out), .bi(multiplexer_9_out), .Hi(precomputation_6_hi), .Gi(precomputation_6_gi),
    .Pi(precomputation_6_pi));
  xor xor_8 (V2, precomputation_6_hi, black_node_8_gigj);
  xor xor_9 (xor_9_out, y0, s);
  HAL hal_4 (.yi_xor_s(xor_9_out), .xi(x0), .Ai(a0_0), .NOT_Ai(a0_1), .Bj(b1_0), .NOT_Bj(b1_1));
  Multiplexer multiplexer_9 (.in0(b2_0), .in1(b2_1), .out(multiplexer_9_out), .sel(s));
  black_node black_node_7 (
    .Gi(precomputation_6_gi), .Gj(black_node_8_gigj), .Pi(precomputation_6_pi), .Pj(black_node_8_pipj),
    .GiGj(black_node_7_gigj));  // open: PiPj
  Multiplexer multiplexer_10 (.in0(a1_0), .in1(a1_1), .out(multiplexer_10_out), .sel(s));
  Multiplexer multiplexer_11 (.in0(b1_0), .in1(b1_1), .out(multiplexer_11_out), .sel(s));
  precomputation precomputation_7 (
    .ai(multiplexer_10_out), .bi(multiplexer_11_out), .Hi(precomputation_7_hi), .Gi(precomputation_7_gi),
    .Pi(precomputation_7_pi));
  black_node black_node_8 (
    .Gi(precomputation_7_gi), .Gj(precomputation_8_gi), .Pi(precomputation_7_pi), .Pj(precomputation_8_pi),
    .GiGj(black_node_8_gigj), .PiPj(black_node_8_pipj));
  xor xor_10 (V1, precomputation_7_hi, precomputation_8_gi);
  Multiplexer multiplexer_12 (.in0(a0_0), .in1(a0_1), .out(multiplexer_12_out), .sel(s));
  precomputation precomputation_8 (
    .ai(multiplexer_12_out), .bi(1'b1), .Hi(V0), .Gi(precomputation_8_gi), .Pi(precomputation_8_pi));

  // Notes on the sheet:
  //   w4
  //   w3
  //   w2
  //   w1
  //   w0
  //   v4
  //   v3
  //   v2
  //   v1
  //   v
  //   0
endmodule

module HAL (
  input  yi_xor_s,
  input  xi,
  output Ai,
  output NOT_Ai,
  output Bj,
  output NOT_Bj
);

  xor xor_1 (Ai, yi_xor_s, xi);
  not not_1 (NOT_Ai, Ai);
  and and_1 (Bj, yi_xor_s, xi);
  or or_1 (NOT_Bj, xi, yi_xor_s);
endmodule

module precomputation (
  input  ai,
  input  bi,
  output Hi,
  output Gi,
  output Pi
);

  xor xor_1 (Hi, ai, bi);
  and and_1 (Gi, ai, bi);
  or or_1 (Pi, ai, bi);
endmodule

module black_node (
  input  Gi,
  input  Gj,
  input  Pi,
  input  Pj,
  output GiGj,
  output PiPj
);

  wire and_1_out;

  and and_1 (and_1_out, Gj, Pi);
  or or_1 (GiGj, Gi, and_1_out);
  and and_2 (PiPj, Pi, Pj);

  // Notes on the sheet:
  //   j=i-1
endmodule

module test (
  input  in_1,
  input  in_2,
  output out_3,
  output out_4,
  output out_5,
  output out_6
);

  // XOR_Gate xor_1 has open pins: in0=in_1, out=open
  HAL hal_1 (.xi(in_2), .Ai(out_5), .NOT_Ai(out_6), .Bj(out_3), .NOT_Bj(out_4));  // open: yi_xor_s
endmodule
